// Logisim project alu.circ as structural Verilog: 1 circuit, main circuit alu
module alu (
  input  [31:0] A,
  input  [31:0] B,
  input  [3:0] ALUSel,
  output [31:0] Result
);

  wire comparator_1_lt;
  wire [31:0] add0, and0, mul0, mulh0, mulhu0, or0, sll0, slt0, sra0, srl0, sub0, xor0;

  Adder #(.width(32)) adder_1 (.a(A), .b(B), .out(add0));  // open: cin, cout
  Shifter #(.width(32)) shifter_1 (.in(A), .\dist (B[4:0]), .out(sll0));
  Comparator #(.width(32)) comparator_1 (.a(A), .b(B), .lt(comparator_1_lt));  // open: gt, eq
  assign xor0 = A ^ B;  // XOR_Gate xor_1, 32 bits wide
  Shifter #(.shift("lr"), .width(32)) shifter_2 (.in(A), .\dist (B[4:0]), .out(srl0));
  assign or0 = A | B;  // OR_Gate or_1, 32 bits wide
  assign and0 = A & B;  // AND_Gate and_1, 32 bits wide
  Multiplier #(.mode("twosComplement"), .width(32)) multiplier_1 (.a(A), .b(B), .out(mul0));  // open: cin, cout
  Multiplier #(.mode("twosComplement"), .width(32)) multiplier_2 (.a(A), .b(B), .cout(mulh0));  // open: out, cin
  Multiplier #(.width(32)) multiplier_3 (.a(A), .b(B), .cout(mulhu0));  // open: out, cin
  Subtractor #(.width(32)) subtractor_1 (.a(A), .b(B), .out(sub0));  // open: bin, bout
  Shifter #(.shift("ar"), .width(32)) shifter_3 (.in(A), .\dist (B[4:0]), .out(sra0));
  assign slt0 = {{31{1'b0}}, comparator_1_lt};  // Bit_Extender bit_extender_1
  Multiplexer #(.enable("false"), .select(4), .width(32)) multiplexer_1 (
    .in0(add0), .in1(sll0), .in2(slt0), .in4(xor0), .in5(srl0), .in6(or0), .in7(and0), .in8(mul0),
    .in9(mulh0), .in11(mulhu0), .in12(sub0), .in13(sra0), .in15(B), .out(Result), .sel(ALUSel));  // open: in3, in10, in14

  // Other names for the same wires on the sheet: bsel0[31:0] = B

  // Notes on the sheet:
  //   INPUTS to your circuit
  //   sel 15
  //   sel 1
  //   Account for output bit length 1
  //   sel 2
  //   sel 4
  //   sel 5
  //   sel 6
  //   sel 7
  //   sel 8
  //   sel 9
  //   sel 11
  //   sel 12
  //   sel 13
  //   sel 0
  //   DON'T CHANGE THE LOCATIONS OF THE INPUTS AND OUTPUTS!
  //   OUTPUT from your circuit
endmodule
