// Logisim project control-logic.circ as structural Verilog: 1 circuit, main circuit control_logic
module control_logic (
  input  [31:0] inst,
  input  BrEq,
  input  BrLt,
  output PCSel,
  output RegWEn,
  output [2:0] ImmSel,
  output BrUn,
  output ASel,
  output BSel,
  output [3:0] ALUSel,
  output MemRW,
  output [1:0] WBSel,
  output CSRSel,
  output CSRWen
);

  wire and_1_out, and_2_out, and_3_out, and_4_out, and_5_out, and_6_out, and_7_out, and_23_out, and_24_out,
       and_25_out, comparator_16_eq, comparator_17_eq, comparator_18_eq, comparator_19_eq, comparator_20_eq,
       comparator_21_eq, comparator_22_eq, comparator_23_eq, comparator_24_eq, comparator_25_eq,
       comparator_26_eq, comparator_27_eq, comparator_28_eq, comparator_29_eq, comparator_30_eq,
       comparator_31_eq, comparator_32_eq, comparator_33_eq, comparator_34_eq, comparator_35_eq,
       comparator_36_eq, comparator_37_eq, comparator_38_eq, comparator_39_eq, comparator_49_eq,
       comparator_50_eq, comparator_53_eq, comparator_54_eq, comparator_55_eq, comparator_56_eq,
       comparator_60_eq, is_add, is_addi, is_and, is_andi, is_auipc, is_beq, is_bge, is_bgeu, is_blt,
       is_bltu, is_bne, is_csrw, is_csrw_type, is_csrwi, is_I_arithmetic, is_I_load, is_jal, is_jalr, is_lb,
       is_lh, is_lui, is_lw, is_mul, is_mulh, is_mulhu, is_or, is_ori, is_R, is_S, is_SB, is_sb_t, is_sh,
       is_sll, is_slli, is_slt, is_slti, is_sra, is_srai, is_srl, is_srli, is_sub, is_sw, is_xor, is_xori,
       not_1_out, not_2_out, not_3_out, not_4_out, not_5_out, or_1_out, or_2_out, or_3_out,
       priority_encoder_1_gs, priority_encoder_2_gs, priority_encoder_3_gs, priority_encoder_4_gs,
       priority_encoder_5_gs, xor_1_out, xor_2_out, xor_3_out;
  wire [4:0] priority_encoder_1_out, priority_encoder_2_out, priority_encoder_3_out, priority_encoder_4_out,
       priority_encoder_5_out;
  wire [5:0] bit_extender_6_out, bit_extender_7_out, bit_extender_8_out, bit_extender_9_out,
       bit_extender_10_out, ROM_input, ROM_input_auipc_filtered, ROM_input_csrw_filtered,
       ROM_input_csrwi_filtered, ROM_input_I_arithmetic, ROM_input_I_arithmetic_filtered,
       ROM_input_I_filtered, ROM_input_I_load, ROM_input_I_load_filtered, ROM_input_jal_filtered,
       ROM_input_jalr_filtered, ROM_input_lui_filtered, ROM_input_R, ROM_input_R_filtered, ROM_input_S,
       ROM_input_S_filtered, ROM_input_SB, ROM_input_SB_filtered;

  ROM #(.addrWidth(6), .dataWidth(16)) rom_1 (
    .addr(ROM_input), .data({RegWEn, ImmSel, BrUn, ASel, BSel, ALUSel, MemRW, WBSel, CSRSel, CSRWen}));
  Comparator #(.width(7)) comparator_1 (.a(7'b1100011), .b(inst[6:0]), .eq(is_SB));  // open: gt, lt
  Comparator #(.width(7)) comparator_2 (.a(7'b0110011), .b(inst[6:0]), .eq(is_R));  // open: gt, lt
  Comparator #(.width(7)) comparator_3 (.a(7'b0100011), .b(inst[6:0]), .eq(is_S));  // open: gt, lt
  Comparator #(.width(7)) comparator_4 (.a(7'b0010111), .b(inst[6:0]), .eq(is_auipc));  // open: gt, lt
  Comparator #(.width(7)) comparator_5 (.a(7'b0110111), .b(inst[6:0]), .eq(is_lui));  // open: gt, lt
  Comparator #(.width(7)) comparator_6 (.a(7'b1101111), .b(inst[6:0]), .eq(is_jal));  // open: gt, lt
  Comparator #(.width(7)) comparator_7 (.a(7'b1110011), .b(inst[6:0]), .eq(is_csrw_type));  // open: gt, lt
  Comparator #(.width(7)) comparator_8 (.a(7'b1100111), .b(inst[6:0]), .eq(is_jalr));  // open: gt, lt
  Comparator #(.width(7)) comparator_9 (.a(7'b0000011), .b(inst[6:0]), .eq(is_I_load));  // open: gt, lt
  Comparator #(.width(7)) comparator_10 (.a(7'b0010011), .b(inst[6:0]), .eq(is_I_arithmetic));  // open: gt, lt
  not not_1 (not_1_out, inst[4]);
  not not_2 (not_2_out, inst[13]);
  not not_3 (not_3_out, inst[14]);
  not not_4 (not_4_out, inst[13]);
  and and_1 (and_1_out, not_2_out, not_3_out);
  xor xor_1 (xor_1_out, inst[12], BrEq);
  xor xor_2 (xor_2_out, inst[12], BrLt);
  and and_2 (and_2_out, not_4_out, inst[14]);
  and and_3 (and_3_out, inst[14], inst[13]);
  xor xor_3 (xor_3_out, inst[12], BrLt);
  and and_4 (and_4_out, not_1_out, inst[6]);
  and and_5 (and_5_out, xor_2_out, and_2_out);
  and and_6 (and_6_out, and_3_out, xor_3_out);
  and and_7 (and_7_out, and_1_out, xor_1_out);
  or or_1 (or_1_out, and_7_out, and_5_out);
  Comparator #(.width(3)) comparator_11 (.a(3'b000), .b(inst[14:12]), .eq(is_sb_t));  // open: gt, lt
  Comparator #(.width(3)) comparator_12 (.a(3'b001), .b(inst[14:12]), .eq(is_sh));  // open: gt, lt
  Comparator #(.width(3)) comparator_13 (.a(3'b010), .b(inst[14:12]), .eq(is_sw));  // open: gt, lt
  or or_2 (or_2_out, or_1_out, and_6_out);
  Comparator #(.width(3)) comparator_14 (.a(3'b001), .b(inst[14:12]), .eq(is_csrw));  // open: gt, lt
  Comparator #(.width(3)) comparator_15 (.a(3'b101), .b(inst[14:12]), .eq(is_csrwi));  // open: gt, lt
  Multiplexer #(.enable("false"), .width(6)) multiplexer_1 (
    .in0({6{1'b0}}), .in1(6'b100011), .out(ROM_input_jalr_filtered), .sel(is_jalr));
  Comparator #(.width(3)) comparator_16 (.a(3'b000), .b(inst[14:12]), .eq(comparator_16_eq));  // open: gt, lt
  Comparator #(.width(7)) comparator_17 (.a({7{1'b0}}), .b(inst[31:25]), .eq(comparator_17_eq));  // open: gt, lt
  Comparator #(.width(3)) comparator_18 (.a(3'b000), .b(inst[14:12]), .eq(comparator_18_eq));  // open: gt, lt
  Comparator #(.width(7)) comparator_19 (.a(7'b0000001), .b(inst[31:25]), .eq(comparator_19_eq));  // open: gt, lt
  Comparator #(.width(3)) comparator_20 (.a(3'b000), .b(inst[14:12]), .eq(comparator_20_eq));  // open: gt, lt
  Comparator #(.width(7)) comparator_21 (.a(7'b0100000), .b(inst[31:25]), .eq(comparator_21_eq));  // open: gt, lt
  Comparator #(.width(3)) comparator_22 (.a(3'b001), .b(inst[14:12]), .eq(comparator_22_eq));  // open: gt, lt
  Comparator #(.width(7)) comparator_23 (.a({7{1'b0}}), .b(inst[31:25]), .eq(comparator_23_eq));  // open: gt, lt
  Comparator #(.width(3)) comparator_24 (.a(3'b001), .b(inst[14:12]), .eq(comparator_24_eq));  // open: gt, lt
  Comparator #(.width(7)) comparator_25 (.a(7'b0000001), .b(inst[31:25]), .eq(comparator_25_eq));  // open: gt, lt
  Comparator #(.width(3)) comparator_26 (.a(3'b011), .b(inst[14:12]), .eq(comparator_26_eq));  // open: gt, lt
  Comparator #(.width(7)) comparator_27 (.a(7'b0000001), .b(inst[31:25]), .eq(comparator_27_eq));  // open: gt, lt
  Comparator #(.width(3)) comparator_28 (.a(3'b010), .b(inst[14:12]), .eq(comparator_28_eq));  // open: gt, lt
  Comparator #(.width(7)) comparator_29 (.a({7{1'b0}}), .b(inst[31:25]), .eq(comparator_29_eq));  // open: gt, lt
  Comparator #(.width(3)) comparator_30 (.a(3'b100), .b(inst[14:12]), .eq(comparator_30_eq));  // open: gt, lt
  Comparator #(.width(7)) comparator_31 (.a({7{1'b0}}), .b(inst[31:25]), .eq(comparator_31_eq));  // open: gt, lt
  Comparator #(.width(3)) comparator_32 (.a(3'b101), .b(inst[14:12]), .eq(comparator_32_eq));  // open: gt, lt
  Comparator #(.width(7)) comparator_33 (.a({7{1'b0}}), .b(inst[31:25]), .eq(comparator_33_eq));  // open: gt, lt
  Comparator #(.width(3)) comparator_34 (.a(3'b101), .b(inst[14:12]), .eq(comparator_34_eq));  // open: gt, lt
  Comparator #(.width(7)) comparator_35 (.a(7'b0100000), .b(inst[31:25]), .eq(comparator_35_eq));  // open: gt, lt
  Comparator #(.width(3)) comparator_36 (.a(3'b110), .b(inst[14:12]), .eq(comparator_36_eq));  // open: gt, lt
  Comparator #(.width(7)) comparator_37 (.a({7{1'b0}}), .b(inst[31:25]), .eq(comparator_37_eq));  // open: gt, lt
  Comparator #(.width(3)) comparator_38 (.a(3'b111), .b(inst[14:12]), .eq(comparator_38_eq));  // open: gt, lt
  Comparator #(.width(7)) comparator_39 (.a({7{1'b0}}), .b(inst[31:25]), .eq(comparator_39_eq));  // open: gt, lt
  Comparator #(.width(3)) comparator_40 (.a(3'b000), .b(inst[14:12]), .eq(is_beq));  // open: gt, lt
  Comparator #(.width(3)) comparator_41 (.a(3'b001), .b(inst[14:12]), .eq(is_bne));  // open: gt, lt
  Comparator #(.width(3)) comparator_42 (.a(3'b100), .b(inst[14:12]), .eq(is_blt));  // open: gt, lt
  Comparator #(.width(3)) comparator_43 (.a(3'b101), .b(inst[14:12]), .eq(is_bge));  // open: gt, lt
  Comparator #(.width(3)) comparator_44 (.a(3'b110), .b(inst[14:12]), .eq(is_bltu));  // open: gt, lt
  Comparator #(.width(3)) comparator_45 (.a(3'b111), .b(inst[14:12]), .eq(is_bgeu));  // open: gt, lt
  Comparator #(.width(3)) comparator_46 (.a(3'b000), .b(inst[14:12]), .eq(is_lb));  // open: gt, lt
  Comparator #(.width(3)) comparator_47 (.a(3'b010), .b(inst[14:12]), .eq(is_lw));  // open: gt, lt
  Comparator #(.width(3)) comparator_48 (.a(3'b000), .b(inst[14:12]), .eq(is_addi));  // open: gt, lt
  Comparator #(.width(3)) comparator_49 (.a(3'b001), .b(inst[14:12]), .eq(comparator_49_eq));  // open: gt, lt
  Comparator #(.width(7)) comparator_50 (.a({7{1'b0}}), .b(inst[31:25]), .eq(comparator_50_eq));  // open: gt, lt
  Comparator #(.width(3)) comparator_51 (.a(3'b010), .b(inst[14:12]), .eq(is_slti));  // open: gt, lt
  Comparator #(.width(3)) comparator_52 (.a(3'b100), .b(inst[14:12]), .eq(is_xori));  // open: gt, lt
  Comparator #(.width(3)) comparator_53 (.a(3'b101), .b(inst[14:12]), .eq(comparator_53_eq));  // open: gt, lt
  Comparator #(.width(7)) comparator_54 (.a({7{1'b0}}), .b(inst[31:25]), .eq(comparator_54_eq));  // open: gt, lt
  Comparator #(.width(3)) comparator_55 (.a(3'b101), .b(inst[14:12]), .eq(comparator_55_eq));  // open: gt, lt
  Comparator #(.width(7)) comparator_56 (.a(7'b0100000), .b(inst[31:25]), .eq(comparator_56_eq));  // open: gt, lt
  Comparator #(.width(3)) comparator_57 (.a(3'b110), .b(inst[14:12]), .eq(is_ori));  // open: gt, lt
  Comparator #(.width(3)) comparator_58 (.a(3'b111), .b(inst[14:12]), .eq(is_andi));  // open: gt, lt
  and and_8 (is_add, comparator_16_eq, comparator_17_eq);
  and and_9 (is_mul, comparator_18_eq, comparator_19_eq);
  and and_10 (is_sub, comparator_20_eq, comparator_21_eq);
  and and_11 (is_sll, comparator_22_eq, comparator_23_eq);
  and and_12 (is_mulh, comparator_24_eq, comparator_25_eq);
  and and_13 (is_mulhu, comparator_26_eq, comparator_27_eq);
  and and_14 (is_slt, comparator_28_eq, comparator_29_eq);
  and and_15 (is_xor, comparator_30_eq, comparator_31_eq);
  and and_16 (is_srl, comparator_32_eq, comparator_33_eq);
  and and_17 (is_sra, comparator_34_eq, comparator_35_eq);
  and and_18 (is_or, comparator_36_eq, comparator_37_eq);
  and and_19 (is_and, comparator_38_eq, comparator_39_eq);
  or or_3 (or_3_out, or_2_out, inst[2]);
  Comparator #(.width(3)) comparator_59 (.a(3'b001), .b(inst[14:12]), .eq(is_lh));  // open: gt, lt
  and and_20 (is_slli, comparator_49_eq, comparator_50_eq);
  and and_21 (is_srli, comparator_53_eq, comparator_54_eq);
  and and_22 (is_srai, comparator_55_eq, comparator_56_eq);
  Comparator #(.width(32)) comparator_60 (.a(inst), .b({32{1'b0}}), .eq(comparator_60_eq));  // open: gt, lt
  Multiplexer #(.enable("false"), .width(6)) multiplexer_2 (
    .in0({6{1'b0}}), .in1(6'b100100), .out(ROM_input_csrw_filtered), .sel(and_23_out));
  and and_23 (and_23_out, is_csrw, is_csrw_type);
  Multiplexer #(.enable("false"), .width(6)) multiplexer_3 (
    .in0({6{1'b0}}), .in1(6'b100101), .out(ROM_input_csrwi_filtered), .sel(and_24_out));
  and and_24 (and_24_out, is_csrwi, is_csrw_type);
  and and_25 (and_25_out, and_4_out, or_3_out);
  not not_5 (not_5_out, comparator_60_eq);
  Multiplexer #(.enable("false"), .width(6)) multiplexer_4 (
    .in0({6{1'b0}}), .in1(6'b100000), .out(ROM_input_auipc_filtered), .sel(is_auipc));
  Multiplexer #(.enable("false"), .width(6)) multiplexer_5 (
    .in0({6{1'b0}}), .in1(6'b100001), .out(ROM_input_lui_filtered), .sel(is_lui));
  Multiplexer #(.enable("false"), .width(6)) multiplexer_6 (
    .in0({6{1'b0}}), .in1(6'b100010), .out(ROM_input_jal_filtered), .sel(is_jal));
  and and_26 (PCSel, and_25_out, not_5_out);
  Priority_Encoder #(.select(5)) priority_encoder_1 (
    .in12(is_lb), .in13(is_lh), .in14(is_lw), .out(priority_encoder_1_out), .gs(priority_encoder_1_gs),
    .en_in(is_I_load));  // open: in0, in1, in2, in3, in4, in5, in6, in7, in8, in9, in10, in11, in15, in16, in17, in18, in19, in20, in21, in22, in23, in24, in25, in26, in27, in28, in29, in30, in31, en_out
  Priority_Encoder #(.select(5)) priority_encoder_2 (
    .in23(is_sb_t), .in24(is_sh), .in25(is_sw), .out(priority_encoder_2_out), .gs(priority_encoder_2_gs),
    .en_in(is_S));  // open: in0, in1, in2, in3, in4, in5, in6, in7, in8, in9, in10, in11, in12, in13, in14, in15, in16, in17, in18, in19, in20, in21, in22, in26, in27, in28, in29, in30, in31, en_out
  assign ROM_input_I_load = {{1{1'b0}}, priority_encoder_1_out};  // Bit_Extender bit_extender_1
  Priority_Encoder #(.select(5)) priority_encoder_3 (
    .in15(is_addi), .in16(is_slli), .in17(is_slti), .in18(is_xori), .in19(is_srli), .in20(is_srai),
    .in21(is_ori), .in22(is_andi), .out(priority_encoder_3_out), .gs(priority_encoder_3_gs),
    .en_in(is_I_arithmetic));  // open: in0, in1, in2, in3, in4, in5, in6, in7, in8, in9, in10, in11, in12, in13, in14, in23, in24, in25, in26, in27, in28, in29, in30, in31, en_out
  Priority_Encoder #(.select(5)) priority_encoder_4 (
    .in26(is_beq), .in27(is_bne), .in28(is_blt), .in29(is_bge), .in30(is_bltu), .in31(is_bgeu),
    .out(priority_encoder_4_out), .gs(priority_encoder_4_gs), .en_in(is_SB));  // open: in0, in1, in2, in3, in4, in5, in6, in7, in8, in9, in10, in11, in12, in13, in14, in15, in16, in17, in18, in19, in20, in21, in22, in23, in24, in25, en_out
  assign ROM_input_S = {{1{1'b0}}, priority_encoder_2_out};  // Bit_Extender bit_extender_2
  assign ROM_input_I_arithmetic = {{1{1'b0}}, priority_encoder_3_out};  // Bit_Extender bit_extender_3
  Priority_Encoder #(.select(5)) priority_encoder_5 (
    .in0(is_add), .in1(is_mul), .in2(is_sub), .in3(is_sll), .in4(is_mulh), .in5(is_mulhu), .in6(is_slt),
    .in7(is_xor), .in8(is_srl), .in9(is_sra), .in10(is_or), .in11(is_and), .out(priority_encoder_5_out),
    .gs(priority_encoder_5_gs), .en_in(is_R));  // open: in12, in13, in14, in15, in16, in17, in18, in19, in20, in21, in22, in23, in24, in25, in26, in27, in28, in29, in30, in31, en_out
  assign ROM_input_SB = {{1{1'b0}}, priority_encoder_4_out};  // Bit_Extender bit_extender_4
  assign ROM_input_R = {{1{1'b0}}, priority_encoder_5_out};  // Bit_Extender bit_extender_5
  assign bit_extender_6_out = {{5{is_I_load}}, priority_encoder_1_gs};  // Bit_Extender bit_extender_6
  assign bit_extender_7_out = {{5{is_SB}}, priority_encoder_4_gs};  // Bit_Extender bit_extender_7
  assign bit_extender_8_out = {{5{is_S}}, priority_encoder_2_gs};  // Bit_Extender bit_extender_8
  assign bit_extender_9_out = {{5{is_I_arithmetic}}, priority_encoder_3_gs};  // Bit_Extender bit_extender_9
  assign bit_extender_10_out = {{5{is_R}}, priority_encoder_5_gs};  // Bit_Extender bit_extender_10
  assign ROM_input = ROM_input_R_filtered | ROM_input_I_filtered | ROM_input_S_filtered | ROM_input_SB_filtered | ROM_input_auipc_filtered | ROM_input_lui_filtered | ROM_input_jal_filtered | ROM_input_jalr_filtered | ROM_input_csrw_filtered | ROM_input_csrwi_filtered;  // OR_Gate or_4, 6 bits wide
  assign ROM_input_I_load_filtered = ROM_input_I_load & bit_extender_6_out;  // AND_Gate and_27, 6 bits wide
  assign ROM_input_S_filtered = ROM_input_S & bit_extender_8_out;  // AND_Gate and_28, 6 bits wide
  assign ROM_input_SB_filtered = ROM_input_SB & bit_extender_7_out;  // AND_Gate and_29, 6 bits wide
  assign ROM_input_I_arithmetic_filtered = ROM_input_I_arithmetic & bit_extender_9_out;  // AND_Gate and_30, 6 bits wide
  assign ROM_input_R_filtered = ROM_input_R & bit_extender_10_out;  // AND_Gate and_31, 6 bits wide
  Multiplexer #(.enable("false"), .width(6)) multiplexer_7 (
    .in0(ROM_input_I_load_filtered), .in1(ROM_input_I_arithmetic_filtered), .out(ROM_input_I_filtered),
    .sel(is_I_arithmetic));

  // Other names for the same wires on the sheet: opcode[6:0] = inst[6:0]; op2 = inst[2]; op4 = inst[4]; op6 = inst[6];
  //   f30 = inst[12]; funct3_csrw[2:0] = inst[14:12]; funct3_I_arithmetic[2:0] = inst[14:12];
  //   funct3_I_load[2:0] = inst[14:12]; funct3_jalr[2:0] = inst[14:12]; funct3_R[2:0] = inst[14:12];
  //   funct3_S[2:0] = inst[14:12]; funct3_SB[2:0] = inst[14:12]; f31 = inst[13]; f32 = inst[14];
  //   funct7_I_arithmetic[6:0] = inst[31:25]; funct7_R[6:0] = inst[31:25]

  // Notes on the sheet:
  //   INPUTS to your circuit
  //   Connect ROM Input here ->
  //   contents of rom_1 (hex, n*v repeats v):
  //   8004 8104 8184 8024 8124 8164 8044 8084 80a4 81a4 80c4 80e4 9208 9208 9208 9204 9224 9244 9284 92a4
  //   93a4 92c4 92e4 2210 2210 2210 4*3600 3e00 3e00 c604 c7e4 d600 9200 201 13e3
  //   ROM FOR CONTROL LOGIC
  //   DON'T CHANGE THE LOCATIONS OF THE INPUTS AND OUTPUTS!
  //   OUTPUT from your circuit
  //   CLOSE
  //   WIRE
  //   TO
  //   USE
  //   ROM
  //   R Type
  //   SB Type
  //   S Type
  //   U type
  //   I type - csrwi
  //   UJ type
  //   CSRW type - csrw
  //   I type - jalr
  //   f30
  //   f31
  //   f32
  //   I Type - load
  //   I Type - arithmetic
  //   op4
  //   op6
  //   op2
  //   Reminder: Use combinational logic for PCSel
  //   -------------------------------------------------------------------------------------------------------------------------------------------------------------------------------------------------------------------------------------------------------------------------------------------------------------------------------------------------------------------------------------------------------------------------------------------------------------------------------------------------
  //   -------------------------------------------------------------------------------------------------------------------------------------------------------------------------------------------------------------------------------------------------------------------------------------------------------------------------------------------------------------------------------------------------------------------------------------------------------------------------------------------------
  //   -------------------------------------------------------------------------------------------------------------------------------------------------------------------------------------------------------------------------------------------------------------------------------------------------------------------------------------------------------------------------------------------------------------------------------------------------------------------------------------------------
  //   -------------------------------------------------------------------------------------------------------------------------------------------------------------------------------------------------------------------------------------------------------------------------------------------------------------------------------------------------------------------------------------------------------------------------------------------------------------------------------------------------
  //   --------------------------------------------------------------------------------------------------------------------------------------------------------------------------------------------------------------------------------------------------------------------------------------------------------------------------------------------------------------------------------------------------------------------------------------------------------------------------------------------------------------------------------------------------------------------------------------------------------------------------------------------------------------------------------------------------------------------------------------------------------
  //   --------------------------------------------------------------------------------------------------------------------------------------------------------------------------------------------------------------------------------------------------------------------------------------------------------------------------------------------------------------------------------------------------------------------------------------------------------------------------------------------------------------------------------------------------------------------------------------------------------------------------------------------------------------------------------------------------------------------------------------------------------
  //   -------------------------------------------------------------------------------------------------------------------------------------------------------------------------------------------------------------------------------------------------------------------------------------------------------------------------------------------------------------------------------------------------------------------------------------------------------------------------------------------------------------------------------------------------------------------------------------------------------------------------------------------------------------------------------------------------------------------------------------------------------------------------------------
  //   --------------------------------------------------------------------------------------------------------------------------------------------------------------------------------------------------------------------------------------------------------------------------------------------------------------------------------------------------------------------------------------------------------------------------------------------------------------------------------------------------------------------------------------------------------------------------------------------------------------------------------------------------------------------------------------------------------------------------------------------------------
  //   -------------------------------------------------------------------------------------------------------------------------------------------------------------------------------------------------------------------------------------------------------------------------------------------------------------------------------------------------------------------------------------------------------------------------------------------------------------------------------------------------
  //   Added AND gate for pipelining
  //   this is light green for addi right now
  //   this is not light green, meaning it is not activated, since the instruction is addi now 
  //   3 more inputs
  //   will need larger or gate later
  //   Will need another one for jalr
endmodule
