// Logisim project cpu.circ as structural Verilog: 1 circuit, main circuit cpu
module cpu (
  input  clk,
  input  [31:0] INSTRUCTION,
  input  [31:0] MEM_READ_DATA,
  output [31:0] MEM_WRITE_ADDRESS,
  output [31:0] PROGRAM_COUNTER,
  output [31:0] ra,
  output [31:0] sp,
  output [31:0] t0,
  output [31:0] t1,
  output [31:0] t2,
  output [31:0] s0,
  output [31:0] s1,
  output [31:0] a0,
  output [31:0] tohost,
  output [3:0] MEM_WRITE_ENABLE,
  output [31:0] MEM_WRITE_DATA
);

  wire and_1_out, and_2_out, and_3_out, and_4_out, and_5_out, and_6_out, and_7_out, and_8_out, and_9_out,
       and_10_out, and_11_out, and_12_out, and_13_out, and_14_out, ASel, BrEq, BrLt, BrUn, BSel,
       comparator_9_eq, comparator_10_eq, comparator_11_eq, comparator_12_eq, comparator_13_eq,
       comparator_14_eq, comparator_15_eq, comparator_16_eq, comparator_17_eq, comparator_18_eq,
       comparator_19_eq, comparator_20_eq, comparator_21_eq, comparator_22_eq, comparator_23_eq, CSRSel,
       CSRWen, is_I_load, is_lb, is_lh, is_lw, is_S, is_sb, is_sh, is_sw, MemRW, not_1_out, not_2_out,
       not_3_out, not_4_out, not_5_out, not_6_out, not_7_out, PCSel, RegWEn;
  wire [1:0] WBSel;
  wire [2:0] funct3_I_load, ImmSel;
  wire [3:0] ALUSel;
  wire [11:0] CSR_address;
  wire [19:0] iNsTrUcTiOn_t;
  wire [31:0] bit_extender_1_out, bit_extender_2_out, bit_extender_3_out, bit_extender_4_out,
       bit_extender_5_out, bit_extender_6_out, imm, load_result, multiplexer_1_out, multiplexer_2_out,
       multiplexer_3_out, multiplexer_4_out, multiplexer_5_out, multiplexer_7_out, multiplexer_8_out,
       multiplexer_9_out, multiplexer_10_out, pC_oNe, PC_plus_four, pC_pLuS_fOuR_t, read_data_1, read_data_2,
       wb;

  Adder #(.width(32)) adder_1 (.a(PROGRAM_COUNTER), .b(32'h4), .out(PC_plus_four));  // open: cin, cout
  Multiplexer #(.enable("false"), .width(32)) multiplexer_1 (
    .in0(read_data_1), .in1(imm), .out(multiplexer_1_out), .sel(CSRSel));
  Multiplexer #(.enable("false"), .width(32)) multiplexer_2 (
    .in0(PC_plus_four), .in1(MEM_WRITE_ADDRESS), .out(multiplexer_2_out), .sel(PCSel));
  Register #(.width(32)) register_1 (.D(PROGRAM_COUNTER), .clk(clk), .Q(pC_oNe));  // open: en, clr
  Register #(.width(32)) PC (.D(multiplexer_2_out), .clk(clk), .Q(PROGRAM_COUNTER));  // open: en, clr
  Multiplexer #(.enable("false"), .width(32)) multiplexer_3 (
    .in0(INSTRUCTION), .in1(32'h13), .out(multiplexer_3_out), .sel(PCSel));
  csr csr_1 (.CSR_address(CSR_address), .CSR_din(multiplexer_1_out), .CSR_WE(CSRWen), .clk(clk), .tohost(tohost));
  Adder #(.width(32)) adder_2 (.a(pC_oNe), .b(32'h4), .out(pC_pLuS_fOuR_t));  // open: cin, cout
  Register #(.width(32)) register_2 (
    .D(multiplexer_3_out), .clk(clk),
    .Q({CSR_address, iNsTrUcTiOn_t[19:15], funct3_I_load, iNsTrUcTiOn_t[11:0]}));  // open: en, clr
  imm_gen imm_gen_1 (
    .inst({CSR_address, iNsTrUcTiOn_t[19:15], funct3_I_load, iNsTrUcTiOn_t[11:0]}), .ImmSel(ImmSel), .imm(imm));
  control_logic control_logic_1 (
    .CSRWen(CSRWen), .PCSel(PCSel), .RegWEn(RegWEn), .ImmSel(ImmSel), .BrUn(BrUn), .ASel(ASel), .BSel(BSel),
    .ALUSel(ALUSel), .MemRW(MemRW), .WBSel(WBSel), .CSRSel(CSRSel),
    .inst({CSR_address, iNsTrUcTiOn_t[19:15], funct3_I_load, iNsTrUcTiOn_t[11:0]}), .BrEq(BrEq), .BrLt(BrLt));
  regfile regfile_1 (
    .rs1(iNsTrUcTiOn_t[19:15]), .rs2(CSR_address[4:0]), .rd(iNsTrUcTiOn_t[11:7]), .Write_Data(wb),
    .RegWEn(RegWEn), .clk(clk), .ra(ra), .sp(sp), .t0(t0), .t1(t1), .t2(t2), .s0(s0), .s1(s1), .a0(a0),
    .Read_Data_1(read_data_1), .Read_Data_2(read_data_2));
  branch_comp branch_comp_1 (.rs1(read_data_1), .rs2(read_data_2), .BrUn(BrUn), .BrEq(BrEq), .BrLt(BrLt));
  Multiplexer #(.enable("false"), .width(32)) multiplexer_4 (
    .in0(read_data_1), .in1(pC_oNe), .out(multiplexer_4_out), .sel(ASel));
  Multiplexer #(.enable("false"), .width(32)) multiplexer_5 (
    .in0(read_data_2), .in1(imm), .out(multiplexer_5_out), .sel(BSel));
  Comparator #(.width(7)) comparator_1 (.a(7'b0000011), .b(iNsTrUcTiOn_t[6:0]), .eq(is_I_load));  // open: gt, lt
  alu alu_1 (.Result(MEM_WRITE_ADDRESS), .A(multiplexer_4_out), .B(multiplexer_5_out), .ALUSel(ALUSel));
  Comparator #(.width(7)) comparator_2 (.a(7'b0100011), .b(iNsTrUcTiOn_t[6:0]), .eq(is_S));  // open: gt, lt
  Comparator #(.width(3)) comparator_3 (.a(3'b000), .b(funct3_I_load), .eq(is_sb));  // open: gt, lt
  Comparator #(.width(3)) comparator_4 (.a(3'b001), .b(funct3_I_load), .eq(is_sh));  // open: gt, lt
  Comparator #(.width(3)) comparator_5 (.a(3'b010), .b(funct3_I_load), .eq(is_sw));  // open: gt, lt
  Comparator #(.width(3)) comparator_6 (.a(3'b000), .b(funct3_I_load), .eq(is_lb));  // open: gt, lt
  Comparator #(.width(3)) comparator_7 (.a(3'b001), .b(funct3_I_load), .eq(is_lh));  // open: gt, lt
  Comparator #(.width(3)) comparator_8 (.a(3'b010), .b(funct3_I_load), .eq(is_lw));  // open: gt, lt
  Multiplexer #(.enable("false"), .select(2), .width(32)) multiplexer_6 (
    .in0(pC_pLuS_fOuR_t), .in1(MEM_WRITE_ADDRESS), .in2(load_result), .out(wb), .sel(WBSel));  // open: in3
  assign bit_extender_1_out = {{24{MEM_READ_DATA[7]}}, MEM_READ_DATA[7:0]};  // Bit_Extender bit_extender_1
  assign bit_extender_2_out = {{24{MEM_READ_DATA[15]}}, MEM_READ_DATA[15:8]};  // Bit_Extender bit_extender_2
  assign bit_extender_3_out = {{24{MEM_READ_DATA[23]}}, MEM_READ_DATA[23:16]};  // Bit_Extender bit_extender_3
  assign bit_extender_4_out = {{24{MEM_READ_DATA[31]}}, MEM_READ_DATA[31:24]};  // Bit_Extender bit_extender_4
  assign bit_extender_5_out = {{16{MEM_READ_DATA[15]}}, MEM_READ_DATA[15:0]};  // Bit_Extender bit_extender_5
  assign bit_extender_6_out = {{16{MEM_READ_DATA[31]}}, MEM_READ_DATA[31:16]};  // Bit_Extender bit_extender_6
  Multiplexer #(.enable("false"), .select(2), .width(32)) multiplexer_7 (
    .in0(bit_extender_1_out), .in1(bit_extender_2_out), .in2(bit_extender_3_out), .in3(bit_extender_4_out),
    .out(multiplexer_7_out), .sel(MEM_WRITE_ADDRESS[1:0]));
  Multiplexer #(.enable("false"), .select(2), .width(32)) multiplexer_8 (
    .in0(bit_extender_5_out), .in2(bit_extender_6_out), .out(multiplexer_8_out), .sel(MEM_WRITE_ADDRESS[1:0]));  // open: in1, in3
  Comparator #(.width(2)) comparator_9 (.a(MEM_WRITE_ADDRESS[1:0]), .b(2'b00), .eq(comparator_9_eq));  // open: gt, lt
  Comparator #(.width(2)) comparator_10 (.a(MEM_WRITE_ADDRESS[1:0]), .b(2'b10), .eq(comparator_10_eq));  // open: gt, lt
  Comparator #(.width(2)) comparator_11 (.a(MEM_WRITE_ADDRESS[1:0]), .b(2'b11), .eq(comparator_11_eq));  // open: gt, lt
  Comparator #(.width(2)) comparator_12 (.a(MEM_WRITE_ADDRESS[1:0]), .b(2'b10), .eq(comparator_12_eq));  // open: gt, lt
  Comparator #(.width(2)) comparator_13 (.a(MEM_WRITE_ADDRESS[1:0]), .b(2'b00), .eq(comparator_13_eq));  // open: gt, lt
  Comparator #(.width(2)) comparator_14 (.a(MEM_WRITE_ADDRESS[1:0]), .b(2'b00), .eq(comparator_14_eq));  // open: gt, lt
  Comparator #(.width(2)) comparator_15 (.a(MEM_WRITE_ADDRESS[1:0]), .b(2'b01), .eq(comparator_15_eq));  // open: gt, lt
  and and_1 (and_1_out, is_sh, comparator_9_eq);
  and and_2 (and_2_out, is_sh, comparator_12_eq);
  Comparator #(.width(1)) comparator_16 (.a(1'b0), .b(MemRW), .eq(comparator_16_eq));  // open: gt, lt
  and and_3 (and_3_out, is_sw, comparator_13_eq);
  Comparator #(.width(1)) comparator_17 (.a(1'b0), .b(MemRW), .eq(comparator_17_eq));  // open: gt, lt
  and and_4 (and_4_out, is_sb, comparator_15_eq);
  Comparator #(.width(1)) comparator_18 (.a(1'b0), .b(MemRW), .eq(comparator_18_eq));  // open: gt, lt
  not not_1 (not_1_out, comparator_19_eq);
  Comparator #(.width(1)) comparator_19 (.a(1'b0), .b(MemRW), .eq(comparator_19_eq));  // open: gt, lt
  and and_5 (and_5_out, is_sb, comparator_10_eq);
  Comparator #(.width(1)) comparator_20 (.a(1'b0), .b(MemRW), .eq(comparator_20_eq));  // open: gt, lt
  and and_6 (and_6_out, is_sb, comparator_11_eq);
  not not_2 (not_2_out, comparator_21_eq);
  Comparator #(.width(1)) comparator_21 (.a(1'b0), .b(MemRW), .eq(comparator_21_eq));  // open: gt, lt
  and and_7 (and_7_out, and_2_out, not_3_out);
  not not_3 (not_3_out, comparator_16_eq);
  and and_8 (and_8_out, and_3_out, not_4_out);
  not not_4 (not_4_out, comparator_17_eq);
  and and_9 (and_9_out, is_sb, comparator_14_eq);
  not not_5 (not_5_out, comparator_22_eq);
  Comparator #(.width(1)) comparator_22 (.a(1'b0), .b(MemRW), .eq(comparator_22_eq));  // open: gt, lt
  and and_10 (and_10_out, and_4_out, not_6_out);
  not not_6 (not_6_out, comparator_18_eq);
  and and_11 (and_11_out, and_1_out, not_1_out);
  and and_12 (and_12_out, and_5_out, not_7_out);
  not not_7 (not_7_out, comparator_20_eq);
  and and_13 (and_13_out, and_6_out, not_2_out);
  and and_14 (and_14_out, and_9_out, not_5_out);
  Multiplexer #(.enable("false"), .select(2), .width(32)) multiplexer_9 (
    .in0({{24{1'b0}}, read_data_2[7:0]}), .in1({{16{1'b0}}, read_data_2[7:0], {8{1'b0}}}),
    .in2({{8{1'b0}}, read_data_2[7:0], {16{1'b0}}}), .in3({read_data_2[7:0], {24{1'b0}}}),
    .out(multiplexer_9_out), .sel(MEM_WRITE_ADDRESS[1:0]));
  Multiplexer #(.enable("false"), .select(2), .width(32)) multiplexer_10 (
    .in0({{16{1'b0}}, read_data_2[15:0]}), .in2({read_data_2[15:0], {16{1'b0}}}), .out(multiplexer_10_out),
    .sel(MEM_WRITE_ADDRESS[1:0]));  // open: in1, in3
  Multiplexer #(.enable("false"), .select(3), .width(32)) multiplexer_11 (
    .in0(multiplexer_7_out), .in1(multiplexer_8_out), .in2(MEM_READ_DATA), .out(load_result),
    .sel(funct3_I_load));  // open: in3, in4, in5, in6, in7
  Comparator #(.width(1)) comparator_23 (.a(MemRW), .b(1'b0), .eq(comparator_23_eq));  // open: gt, lt
  Multiplexer #(.enable("false"), .select(3), .width(32)) multiplexer_12 (
    .in0(multiplexer_9_out), .in1(multiplexer_10_out), .in2(read_data_2), .out(MEM_WRITE_DATA),
    .sel(funct3_I_load));  // open: in3, in4, in5, in6, in7
  Priority_Encoder #(.select(4)) priority_encoder_1 (
    .in0(comparator_23_eq), .in1(and_14_out), .in2(and_10_out), .in3(and_11_out), .in4(and_12_out),
    .in8(and_13_out), .in12(and_7_out), .in15(and_8_out), .out(MEM_WRITE_ENABLE));  // open: in5, in6, in7, in9, in10, in11, in13, in14, gs, en_out, en_in

  // Other names for the same wires on the sheet: read_data_2_fifteen_zero[15:0] = read_data_2[15:0];
  //   read_data_2_seven_zero[7:0] = read_data_2[7:0]; opcode[6:0] = iNsTrUcTiOn_t[6:0]; rd[4:0] = iNsTrUcTiOn_t[11:7];
  //   funct3_S[2:0] = funct3_I_load; iNsTrUcTiOn_t (some bits) = {CSR_address, funct3_I_load};
  //   rs1[4:0] = iNsTrUcTiOn_t[19:15]; rs2[4:0] = CSR_address[4:0]; bottom_two_bits[1:0] = MEM_WRITE_ADDRESS[1:0];
  //   Result[31:0] = MEM_WRITE_ADDRESS

  // Notes on the sheet:
  //   Output to IMEM
  //   is not a branch
  //   is a branch
  //   IMEM (do **NOT** move this)
  //   Inputs from IMEM
  //   It is OK to move the PC, RegFile, ALU, MEM, Branch Comp, Imm Gen, and Control Logic to wherever is most convenient for you when constructing your CPU, and to delete this text
  //   Inputs/Outputs for testing. Do **NOT** move these.
  //   RegWEn was hard-coded to 1 for addi
  //   Bitmask calculation for store
  //   I Type - load
  //   If MemRW is zero, we output zero. Else we output based on the opcode and the bottom two bits
  //   S Type
  //   Outputs To DMEM
  //   DMEM (do **NOT** move this)
  //   alusel was hard-coded to 0000 for addi 
  //   Inputs From DMEM
  //   --------------------------------------------------------------------------------------------------------------------------------------------------------------------------------------------------------------------------------------------------------------------------------------------------------------------------------------------------------------------------------------------------------------------------------------------------------------------------------------------------------------------------------------------------------------------------------------------------------------------------------------------------------------------------------------------------------------------------------------------------------
  //   --------------------------------------------------------------------------------------------------------------------------------------------------------------------------------------------------------------------------------------------------------------------------------------------------------------------------------------------------------------------------------------------------------------------------------------------------------------------------------------------------------------------------------------------------------------------------------------------------------------------------------------------------------------------------------------------------------------------------------------------------------
endmodule
