// Logisim project imm-gen.circ as structural Verilog: 1 circuit, main circuit imm_gen
module imm_gen (
  input  [31:0] inst,
  input  [2:0] ImmSel,
  output [31:0] imm
);

  wire and_4_out, comparator_16_eq, comparator_17_eq, comparator_20_eq, comparator_21_eq, comparator_22_eq,
       comparator_23_eq, is_addi, is_andi, is_auipc, is_csrw, is_csrw_type, is_csrwi, is_I_arithmetic,
       is_I_load, is_jal, is_jalr, is_lb, is_lh, is_lui, is_lw, is_ori, is_S, is_SB, is_slli, is_slti,
       is_srai, is_srli, is_xori, or_1_out, or_2_out;
  wire [31:0] imm_csrwi, imm_I_type, imm_jalr, imm_load, imm_no_shift, imm_shift, multiplexer_2_out,
       multiplexer_3_out, multiplexer_4_out;
  wire [31:11] imm_S_type;
  wire [31:12] imm_SB_type;
  wire [31:20] imm_UJ_type;

  Comparator #(.width(7)) comparator_1 (.a(7'b1110011), .b(inst[6:0]), .eq(is_csrw_type));  // open: gt, lt
  Comparator #(.width(7)) comparator_2 (.a(7'b1100111), .b(inst[6:0]), .eq(is_jalr));  // open: gt, lt
  Comparator #(.width(7)) comparator_3 (.a(7'b0000011), .b(inst[6:0]), .eq(is_I_load));  // open: gt, lt
  Comparator #(.width(7)) comparator_4 (.a(7'b0010011), .b(inst[6:0]), .eq(is_I_arithmetic));  // open: gt, lt
  Comparator #(.width(7)) comparator_5 (.a(7'b1100011), .b(inst[6:0]), .eq(is_S));  // open: gt, lt
  Comparator #(.width(7)) comparator_6 (.a(7'b0010111), .b(inst[6:0]), .eq(is_auipc));  // open: gt, lt
  Comparator #(.width(7)) comparator_7 (.a(7'b0110111), .b(inst[6:0]), .eq(is_lui));  // open: gt, lt
  Comparator #(.width(7)) comparator_8 (.a(7'b1101111), .b(inst[6:0]), .eq(is_jal));  // open: gt, lt
  Comparator #(.width(7)) comparator_9 (.a(7'b1100011), .b(inst[6:0]), .eq(is_SB));  // open: gt, lt
  Comparator #(.width(3)) comparator_10 (.a(3'b001), .b(inst[14:12]), .eq(is_csrw));  // open: gt, lt
  Comparator #(.width(3)) comparator_11 (.a(3'b101), .b(inst[14:12]), .eq(is_csrwi));  // open: gt, lt
  Comparator #(.width(3)) comparator_12 (.a(3'b000), .b(inst[14:12]), .eq(is_lb));  // open: gt, lt
  Comparator #(.width(3)) comparator_13 (.a(3'b001), .b(inst[14:12]), .eq(is_lh));  // open: gt, lt
  Comparator #(.width(3)) comparator_14 (.a(3'b010), .b(inst[14:12]), .eq(is_lw));  // open: gt, lt
  Comparator #(.width(3)) comparator_15 (.a(3'b000), .b(inst[14:12]), .eq(is_addi));  // open: gt, lt
  Comparator #(.width(3)) comparator_16 (.a(3'b001), .b(inst[14:12]), .eq(comparator_16_eq));  // open: gt, lt
  Comparator #(.width(7)) comparator_17 (.a({7{1'b0}}), .b(inst[31:25]), .eq(comparator_17_eq));  // open: gt, lt
  Comparator #(.width(3)) comparator_18 (.a(3'b010), .b(inst[14:12]), .eq(is_slti));  // open: gt, lt
  Comparator #(.width(3)) comparator_19 (.a(3'b100), .b(inst[14:12]), .eq(is_xori));  // open: gt, lt
  Comparator #(.width(3)) comparator_20 (.a(3'b101), .b(inst[14:12]), .eq(comparator_20_eq));  // open: gt, lt
  Comparator #(.width(7)) comparator_21 (.a({7{1'b0}}), .b(inst[31:25]), .eq(comparator_21_eq));  // open: gt, lt
  Comparator #(.width(3)) comparator_22 (.a(3'b101), .b(inst[14:12]), .eq(comparator_22_eq));  // open: gt, lt
  Comparator #(.width(7)) comparator_23 (.a(7'b0100000), .b(inst[31:25]), .eq(comparator_23_eq));  // open: gt, lt
  Comparator #(.width(3)) comparator_24 (.a(3'b110), .b(inst[14:12]), .eq(is_ori));  // open: gt, lt
  Comparator #(.width(3)) comparator_25 (.a(3'b111), .b(inst[14:12]), .eq(is_andi));  // open: gt, lt
  and and_1 (is_slli, comparator_16_eq, comparator_17_eq);
  and and_2 (is_srli, comparator_20_eq, comparator_21_eq);
  and and_3 (is_srai, comparator_22_eq, comparator_23_eq);
  Multiplexer #(.enable("false"), .select(3), .width(32)) multiplexer_1 (
    .in1(imm_I_type), .in2({imm_S_type, inst[30:25], inst[11:7]}),
    .in3({imm_SB_type, inst[7], inst[30:25], inst[11:8], 1'b0}), .in4({inst[31:12], {12{1'b0}}}),
    .in5({imm_UJ_type, inst[19:12], inst[20], inst[30:21], 1'b0}), .out(imm), .sel(ImmSel));  // open: in0, in6, in7
  assign imm_csrwi = {{27{1'b0}}, inst[19:15]};  // Bit_Extender bit_extender_1
  assign imm_jalr = {{20{inst[31]}}, inst[31:20]};  // Bit_Extender bit_extender_2
  assign imm_load = {{20{inst[31]}}, inst[31:20]};  // Bit_Extender bit_extender_3
  assign imm_no_shift = {{20{inst[31]}}, inst[31:20]};  // Bit_Extender bit_extender_4
  assign imm_shift = {{27{inst[24]}}, inst[24:20]};  // Bit_Extender bit_extender_5
  assign imm_S_type = {{20{inst[31]}}, inst[31]};  // Bit_Extender bit_extender_6
  assign imm_SB_type = {{19{inst[31]}}, inst[31]};  // Bit_Extender bit_extender_7
  assign imm_UJ_type = {{11{inst[31]}}, inst[31]};  // Bit_Extender bit_extender_8
  Multiplexer #(.enable("false"), .width(32)) multiplexer_2 (
    .in0(imm_no_shift), .in1(imm_shift), .out(multiplexer_2_out), .sel(or_1_out));
  or or_1 (or_1_out, is_slli, is_srli, is_srai);
  Multiplexer #(.enable("false"), .width(32)) multiplexer_3 (
    .in0(multiplexer_2_out), .in1(imm_load), .out(multiplexer_3_out), .sel(or_2_out));
  or or_2 (or_2_out, is_lb, is_lh, is_lw);
  Multiplexer #(.enable("false"), .width(32)) multiplexer_4 (
    .in0(multiplexer_3_out), .in1(imm_jalr), .out(multiplexer_4_out), .sel(is_jalr));
  Multiplexer #(.enable("false"), .width(32)) multiplexer_5 (
    .in0(multiplexer_4_out), .in1(imm_csrwi), .out(imm_I_type), .sel(and_4_out));
  and and_4 (and_4_out, is_csrwi, is_csrw_type);

  // Other names for the same wires on the sheet: imm_S_type[10:0] = {inst[30:25], inst[11:7]};
  //   imm_SB_type[11:1] = {inst[7], inst[30:25], inst[11:8]}; funct7_I_arithmetic[6:0] = inst[31:25];
  //   imm_U_type[31:12] = inst[31:12]; imm_UJ_type[19:1] = {inst[19:12], inst[20], inst[30:21]};
  //   funct3_csrw[2:0] = inst[14:12]; funct3_I_arithmetic[2:0] = inst[14:12]; funct3_I_load[2:0] = inst[14:12];
  //   funct3_jalr[2:0] = inst[14:12]; opcode[6:0] = inst[6:0]

  // Notes on the sheet:
  //   INPUTS to your circuit
  //   I type - csrw
  //   I type - jalr
  //   I Type - load
  //   I Type - arithmetic
  //   UJ type
  //   U type
  //   DON'T CHANGE THE LOCATIONS OF THE INPUTS AND OUTPUTS!
  //   S Type
  //   SB Type
  //   OUTPUT from your circuit
  //   --------------------------------------------------------------------------------------------------------------------------------------------------------------------------------------------------------------------------------------------------------------------------------------------------------------------------------------------------------------------------------------------------------------------------------------------------------------------------------------------------------------------------------------------------------------------------------------------------------------------------------------------------------------------------------------------------------------------------------------------------------
  //   --------------------------------------------------------------------------------------------------------------------------------------------------------------------------------------------------------------------------------------------------------------------------------------------------------------------------------------------------------------------------------------------------------------------------------------------------------------------------------------------------------------------------------------------------------------------------------------------------------------------------------------------------------------------------------------------------------------------------------------------------------
  //   --------------------------------------------------------------------------------------------------------------------------------------------------------------------------------------------------------------------------------------------------------------------------------------------------------------------------------------------------------------------------------------------------------------------------------------------------------------------------------------------------------------------------------------------------------------------------------------------------------------------------------------------------------------------------------------------------------------------------------------------------------
  //   I-type load
  //   I-type arithmetic
  //   S Type
  //   U type
  //   U type - auipc
  //   --------------------------------------------------------------------------------------------------------------------------------------------------------------------------------------------------------------------------------------------------------------------------------------------------------------------------------------------------------------------------------------------------------------------------------------------------------------------------------------------------------------------------------------------------------------------------------------------------------------------------------------------------------------------------------------------------------------------------------------------------------
  //   --------------------------------------------------------------------------------------------------------------------------------------------------------------------------------------------------------------------------------------------------------------------------------------------------------------------------------------------------------------------------------------------------------------------------------------------------------------------------------------------------------------------------------------------------------------------------------------------------------------------------------------------------------------------------------------------------------------------------------------------------------
  //   SB Type
  //   --------------------------------------------------------------------------------------------------------------------------------------------------------------------------------------------------------------------------------------------------------------------------------------------------------------------------------------------------------------------------------------------------------------------------------------------------------------------------------------------------------------------------------------------------------------------------------------------------------------------------------------------------------------------------------------------------------------------------------------------------------
  //   --------------------------------------------------------------------------------------------------------------------------------------------------------------------------------------------------------------------------------------------------------------------------------------------------------------------------------------------------------------------------------------------------------------------------------------------------------------------------------------------------------------------------------------------------------------------------------------------------------------------------------------------------------------------------------------------------------------------------------------------------------
  //   --------------------------------------------------------------------------------------------------------------------------------------------------------------------------------------------------------------------------------------------------------------------------------------------------------------------------------------------------------------------------------------------------------------------------------------------------------------------------------------------------------------------------------------------------------------------------------------------------------------------------------------------------------------------------------------------------------------------------------------------------------
  //   confirm that this sign extension scheme works
  //   Checks done down below
  //   Checks done down below
  //   Checks done down below
  //   Might need more gates here later for other I types
endmodule
