// Logisim project regfile.circ as structural Verilog: 1 circuit, main circuit regfile
module regfile (
  input  [4:0] rs1,
  input  [4:0] rs2,
  input  [4:0] rd,
  input  [31:0] Write_Data,
  input  RegWEn,
  input  clk,
  output [31:0] ra,
  output [31:0] sp,
  output [31:0] t0,
  output [31:0] t1,
  output [31:0] t2,
  output [31:0] s0,
  output [31:0] s1,
  output [31:0] a0,
  output [31:0] Read_Data_1,
  output [31:0] Read_Data_2
);

  wire write_en0, write_en1, write_en2, write_en3, write_en4, write_en5, write_en6, write_en7, write_en8,
       write_en9, write_en10, write_en11, write_en12, write_en13, write_en14, write_en15, write_en16,
       write_en17, write_en18, write_en19, write_en20, write_en21, write_en22, write_en23, write_en24,
       write_en25, write_en26, write_en27, write_en28, write_en29, write_en30, write_en31;
  wire [31:0] out0, out3, out4, out11, out12, out13, out14, out15, out16, out17, out18, out19, out20, out21,
       out22, out23, out24, out25, out26, out27, out28, out29, out30, out31;

  Register #(.width(32)) x0 (.D(Write_Data), .en(write_en0), .clk(clk), .Q(out0), .clr(1'b1));
  Register #(.width(32)) x8 (.D(Write_Data), .en(write_en8), .clk(clk), .Q(s0));  // open: clr
  Register #(.width(32)) x16 (.D(Write_Data), .en(write_en16), .clk(clk), .Q(out16));  // open: clr
  Register #(.width(32)) x24 (.D(Write_Data), .en(write_en24), .clk(clk), .Q(out24));  // open: clr
  Demultiplexer #(.enable("false"), .select(5)) demultiplexer_1 (
    .out0(write_en0), .out1(write_en1), .out2(write_en2), .out3(write_en3), .out4(write_en4),
    .out5(write_en5), .out6(write_en6), .out7(write_en7), .out8(write_en8), .out9(write_en9),
    .out10(write_en10), .out11(write_en11), .out12(write_en12), .out13(write_en13), .out14(write_en14),
    .out15(write_en15), .out16(write_en16), .out17(write_en17), .out18(write_en18), .out19(write_en19),
    .out20(write_en20), .out21(write_en21), .out22(write_en22), .out23(write_en23), .out24(write_en24),
    .out25(write_en25), .out26(write_en26), .out27(write_en27), .out28(write_en28), .out29(write_en29),
    .out30(write_en30), .out31(write_en31), .in(RegWEn), .sel(rd));
  Register #(.width(32)) x1 (.D(Write_Data), .en(write_en1), .clk(clk), .Q(ra));  // open: clr
  Register #(.width(32)) x9 (.D(Write_Data), .en(write_en9), .clk(clk), .Q(s1));  // open: clr
  Register #(.width(32)) x17 (.D(Write_Data), .en(write_en17), .clk(clk), .Q(out17));  // open: clr
  Register #(.width(32)) x25 (.D(Write_Data), .en(write_en25), .clk(clk), .Q(out25));  // open: clr
  Register #(.width(32)) x2 (.D(Write_Data), .en(write_en2), .clk(clk), .Q(sp));  // open: clr
  Register #(.width(32)) x10 (.D(Write_Data), .en(write_en10), .clk(clk), .Q(a0));  // open: clr
  Register #(.width(32)) x18 (.D(Write_Data), .en(write_en18), .clk(clk), .Q(out18));  // open: clr
  Register #(.width(32)) x26 (.D(Write_Data), .en(write_en26), .clk(clk), .Q(out26));  // open: clr
  Register #(.width(32)) x3 (.D(Write_Data), .en(write_en3), .clk(clk), .Q(out3));  // open: clr
  Register #(.width(32)) x11 (.D(Write_Data), .en(write_en11), .clk(clk), .Q(out11));  // open: clr
  Register #(.width(32)) x19 (.D(Write_Data), .en(write_en19), .clk(clk), .Q(out19));  // open: clr
  Register #(.width(32)) x27 (.D(Write_Data), .en(write_en27), .clk(clk), .Q(out27));  // open: clr
  Multiplexer #(.enable("false"), .select(5), .width(32)) multiplexer_1 (
    .in0(out0), .in1(ra), .in2(sp), .in3(out3), .in4(out4), .in5(t0), .in6(t1), .in7(t2), .in8(s0), .in9(s1),
    .in10(a0), .in11(out11), .in12(out12), .in13(out13), .in14(out14), .in15(out15), .in16(out16),
    .in17(out17), .in18(out18), .in19(out19), .in20(out20), .in21(out21), .in22(out22), .in23(out23),
    .in24(out24), .in25(out25), .in26(out26), .in27(out27), .in28(out28), .in29(out29), .in30(out30),
    .in31(out31), .out(Read_Data_1), .sel(rs1));
  Register #(.width(32)) x4 (.D(Write_Data), .en(write_en4), .clk(clk), .Q(out4));  // open: clr
  Register #(.width(32)) x12 (.D(Write_Data), .en(write_en12), .clk(clk), .Q(out12));  // open: clr
  Register #(.width(32)) x20 (.D(Write_Data), .en(write_en20), .clk(clk), .Q(out20));  // open: clr
  Register #(.width(32)) x28 (.D(Write_Data), .en(write_en28), .clk(clk), .Q(out28));  // open: clr
  Register #(.width(32)) x5 (.D(Write_Data), .en(write_en5), .clk(clk), .Q(t0));  // open: clr
  Register #(.width(32)) x13 (.D(Write_Data), .en(write_en13), .clk(clk), .Q(out13));  // open: clr
  Register #(.width(32)) x21 (.D(Write_Data), .en(write_en21), .clk(clk), .Q(out21));  // open: clr
  Register #(.width(32)) x29 (.D(Write_Data), .en(write_en29), .clk(clk), .Q(out29));  // open: clr
  Multiplexer #(.enable("false"), .select(5), .width(32)) multiplexer_2 (
    .in0(out0), .in1(ra), .in2(sp), .in3(out3), .in4(out4), .in5(t0), .in6(t1), .in7(t2), .in8(s0), .in9(s1),
    .in10(a0), .in11(out11), .in12(out12), .in13(out13), .in14(out14), .in15(out15), .in16(out16),
    .in17(out17), .in18(out18), .in19(out19), .in20(out20), .in21(out21), .in22(out22), .in23(out23),
    .in24(out24), .in25(out25), .in26(out26), .in27(out27), .in28(out28), .in29(out29), .in30(out30),
    .in31(out31), .out(Read_Data_2), .sel(rs2));
  Register #(.width(32)) x6 (.D(Write_Data), .en(write_en6), .clk(clk), .Q(t1));  // open: clr
  Register #(.width(32)) x14 (.D(Write_Data), .en(write_en14), .clk(clk), .Q(out14));  // open: clr
  Register #(.width(32)) x22 (.D(Write_Data), .en(write_en22), .clk(clk), .Q(out22));  // open: clr
  Register #(.width(32)) x30 (.D(Write_Data), .en(write_en30), .clk(clk), .Q(out30));  // open: clr
  Register #(.width(32)) x7 (.D(Write_Data), .en(write_en7), .clk(clk), .Q(t2));  // open: clr
  Register #(.width(32)) x15 (.D(Write_Data), .en(write_en15), .clk(clk), .Q(out15));  // open: clr
  Register #(.width(32)) x23 (.D(Write_Data), .en(write_en23), .clk(clk), .Q(out23));  // open: clr
  Register #(.width(32)) x31 (.D(Write_Data), .en(write_en31), .clk(clk), .Q(out31));  // open: clr

  // Other names for the same wires on the sheet: out1[31:0] = ra; out2[31:0] = sp; out5[31:0] = t0; out6[31:0] = t1;
  //   out7[31:0] = t2; out8[31:0] = s0; out9[31:0] = s1; out10[31:0] = a0; read_data1[31:0] = Read_Data_1;
  //   read_data2[31:0] = Read_Data_2; read_reg1[4:0] = rs1; read_reg2[4:0] = rs2; write_en = RegWEn;
  //   write_reg[4:0] = rd

  // Notes on the sheet:
  //   INPUTS to your circuit
  //   DON'T CHANGE THE LOCATIONS OF THE INPUTS AND OUTPUTS!
  //   These are DEBUG/TEST outputs from your circuit.
  //   OUTPUTS from your circuit
endmodule
